# Fritzing sketch ModuleDIMJV (saved by Fritzing 0.9.9b)
circuit board: 12.5312cm x 12.5018cm
breadboards: 1

parts:
  R1 = Resistor [tolerance=±5% power=0.25 resistance=220 package=THT]
  J1 = RJ11 Jack [package=rj11-6]
  U1 = TLP621 [package=THT]
  C1 = Capacitor Polarized [package=cpol-radial-1000uf-25v]
  C2 = Capacitor [package=cap-pth-small2]
  U2 = TLP621 [package=THT]
  U3 = TLP621 [package=THT]
  U4 = TLP621 [package=THT]
  U5 = TLP621 [package=THT]
  U6 = TLP621 [package=THT]
  R2 = Resistor [tolerance=±5% power=0.25 resistance=220 package=THT]
  R3 = Resistor [tolerance=±5% power=0.25 resistance=220 package=THT]
  R5 = Resistor [tolerance=±5% power=0.25 resistance=220 package=THT]
  R6 = Resistor [tolerance=±5% power=0.25 resistance=220 package=THT]
  R7 = Resistor [tolerance=±5% power=0.25 resistance=220 package=THT]
  J3 = RJ11 Jack [package=rj11-6]
  J4 = RJ11 Jack [package=rj11-6]
  J5 = RJ11 Jack [package=rj11-6]
  J6 = RJ11 Jack [package=rj11-6]
  J7 = RJ11 Jack [package=rj11-6]
  Q2 = TRANSISTOR_NPN [package=to-92]
  J8 = Camdenboss CTB0158-8 [part_number=CTB0158-8 package=THT]
  R8 = Resistor [tolerance=±5% power=0.25 resistance=220 package=THT]
  R9 = Resistor [tolerance=±5% power=0.25 resistance=220 package=THT]
  R10 = Resistor [tolerance=±5% power=0.25 resistance=220 package=THT]
  R11 = Resistor [tolerance=±5% power=0.25 resistance=220 package=THT]
  R12 = Resistor [tolerance=±5% power=0.25 resistance=220 package=THT]
  R13 = Resistor [tolerance=±5% power=0.25 resistance=220 package=THT]
  R14 = Resistor [tolerance=±5% power=0.25 resistance=220 package=THT]
  R15 = Resistor [tolerance=±5% power=0.25 resistance=220 package=THT]
  R16 = Resistor [tolerance=±5% power=0.25 resistance=220 package=THT]
  Q3 = TRANSISTOR_NPN [package=to-92]
  Q4 = TRANSISTOR_NPN [package=to-92]
  Q5 = TRANSISTOR_NPN [package=to-92]
  Q6 = TRANSISTOR_NPN [package=to-92]
  Q7 = TRANSISTOR_NPN [package=to-92]
  Q8 = TRANSISTOR_NPN [package=to-92]
  Q9 = TRANSISTOR_NPN [package=to-92]
  Q10 = TRANSISTOR_NPN [package=to-92]
  R4 = Resistor [tolerance=±5% power=0.25 resistance=220 package=THT]
  J2 = Camdenboss CTB0158-2 [part_number=CTB0158-2 package=THT]
  Composant1 = Arduino Mega 2560 (Rev3)

nets (from the pcb view):
  N1: R1.Pin_0, Q2.B
  N2: R1.Pin_1, Composant1.D13_PWM
  N3: J1.1, C1.+, C2.2, J3.1, J4.1, J5.1, J6.1, J7.1, J2.pin1, Composant1.VIN
  N4: J1.3, Q2.C
  N5: U1.Pin_1, Composant1.A10
  N6: U1.Pin_2, U2.Pin_2, U3.Pin_2, U4.Pin_2, U5.Pin_2, U6.Pin_2, R8.Pin_1
  N7: U1.Pin_4, U2.Pin_4, U3.Pin_4, U4.Pin_4, U5.Pin_4, U6.Pin_4, J8.pin1
  N8: U1.Pin_3, R2.Pin_0
  N9: C1.-, C2.1, Q2.E, Q3.E, Q4.E, Q5.E, Q6.E, Q7.E, Q8.E, Q9.E, Q10.E, J2.pin2, Composant1.GND
  N10: U2.Pin_1, Composant1.A11
  N11: U2.Pin_3, R3.Pin_0
  N12: U3.Pin_1, Composant1.A12
  N13: U3.Pin_3, R4.Pin_0
  N14: U4.Pin_1, Composant1.A13
  N15: U4.Pin_3, R5.Pin_0
  N16: U5.Pin_1, Composant1.A14
  N17: U5.Pin_3, R6.Pin_0
  N18: U6.Pin_1, Composant1.A15
  N19: U6.Pin_3, R7.Pin_0
  N20: R2.Pin_1, J8.pin3
  N21: R3.Pin_1, J8.pin4
  N22: R5.Pin_1, J8.pin6
  N23: R6.Pin_1, J8.pin7
  N24: R7.Pin_1, J8.pin8
  N25: J3.3, Q3.C
  N26: J4.3, Q4.C
  N27: J5.3, Q7.C
  N28: J6.3, Q10.C
  N29: J8.pin5, R4.Pin_1
  N30: R8.Pin_0, Composant1.3V3
  N31: R9.Pin_0, Q3.B
  N32: R9.Pin_1, Composant1.D12_PWM
  N33: R10.Pin_0, Q4.B
  N34: R10.Pin_1, Composant1.D11_PWM
  N35: R11.Pin_0, Q5.B
  N36: R11.Pin_1, Composant1.D5_PWM
  N37: R12.Pin_0, Q6.B
  N38: R12.Pin_1, Composant1.D4_PWM
  N39: R13.Pin_0, Q7.B
  N40: R13.Pin_1, Composant1.D2_PWM
  N41: R14.Pin_0, Q8.B
  N42: R15.Pin_0, Q9.B
  N43: R16.Pin_0, Q10.B
  N44: R16.Pin_1, Composant1.D3_PWM

notes:
  Frederic H-G DIM V1 mai22
  No1
  No2
  No3
  No4
  No5
  No6
