# Fritzing sketch DIM_V2 (saved by Fritzing 0.9.9b)
circuit board: 12.5cm x 12.5cm
breadboards: 1

parts:
  J7 = RJ11 Jack [package=rj11-6]
  J6 = RJ11 Jack [package=rj11-6]
  J5 = RJ11 Jack [package=rj11-6]
  J4 = RJ11 Jack [package=rj11-6]
  J3 = RJ11 Jack [package=rj11-6]
  C3 = Capacitor [package=cap-pth-small2]
  Q3 = TRANSISTOR_NPN [package=to-92]
  Q4 = TRANSISTOR_NPN [package=to-92]
  Q5 = TRANSISTOR_NPN [package=to-92]
  Q6 = TRANSISTOR_NPN [package=to-92]
  Q7 = TRANSISTOR_NPN [package=to-92]
  Q8 = TRANSISTOR_NPN [package=to-92]
  R1 = Resistor [tolerance=±5% power=0.25 resistance=220 package=THT]
  R2 = Resistor [tolerance=±5% power=0.25 resistance=220 package=THT]
  R3 = Resistor [tolerance=±5% power=0.25 resistance=220 package=THT]
  R4 = Resistor [tolerance=±5% power=0.25 resistance=220 package=THT]
  R5 = Resistor [tolerance=±5% power=0.25 resistance=220 package=THT]
  R6 = Resistor [tolerance=±5% power=0.25 resistance=220 package=THT]
  R8 = Resistor [tolerance=±5% power=0.25 resistance=10k package=THT]
  R9 = Resistor [tolerance=±5% power=0.25 resistance=10k package=THT]
  R10 = Resistor [tolerance=±5% power=0.25 resistance=10k package=THT]
  R11 = Resistor [tolerance=±5% power=0.25 resistance=10k package=THT]
  R12 = Resistor [tolerance=±5% power=0.25 resistance=10k package=THT]
  R13 = Resistor [tolerance=±5% power=0.25 resistance=10k package=THT]
  J8 = Camdenboss CTB0158-8 [part_number=CTB0158-8 package=THT]
  J2 = RJ11 Jack [package=rj11-6]
  Q9 = TRANSISTOR_NPN [package=to-92]
  R7 = Resistor [tolerance=±5% power=0.25 resistance=220 package=THT]
  J1 = Camdenboss CTB0158-2 [part_number=CTB0158-2 package=THT]
  U6 = TLP621 [package=THT]
  U7 = TLP621 [package=THT]
  U8 = TLP621 [package=THT]
  U9 = TLP621 [package=THT]
  U10 = TLP621 [package=THT]
  U11 = TLP621 [package=THT]
  C1 = Capacitor Polarized [package=cpol-radial-1000uf-25v]
  Arduino_MEGA_2560 = Arduino Mega 2560 (Rev3)

nets:
  12V: J7.1, J6.1, J5.1, J4.1, J3.1, C3.2, J2.1, J1.pin1, C1.+, Arduino_MEGA_2560.VIN
  N1: J7.3, J7.5, Q8.C
  N2: J6.3, J6.5, Q7.C
  N3: J5.3, J5.5, Q6.C
  N4: J4.3, J4.5, Q5.C
  N5: J3.3, J3.5, Q4.C
  GND: C3.1, Q3.E, Q4.E, Q5.E, Q6.E, Q7.E, Q8.E, J1.pin2, U6.Pin_3, U7.Pin_3, U8.Pin_3, U9.Pin_3, U10.Pin_3, U11.Pin_3, C1.-, Arduino_MEGA_2560.GND
  N6: Q3.B, R1.Pin_0
  N7: Q3.C, J2.3, J2.5
  N8: Q4.B, R2.Pin_0
  N9: Q5.B, R3.Pin_0
  N10: Q6.B, R4.Pin_0
  N11: Q7.B, R5.Pin_0
  N12: Q8.B, R6.Pin_0
  N13: R1.Pin_1, Arduino_MEGA_2560.D13_PWM
  N14: R2.Pin_1, Arduino_MEGA_2560.D12_PWM
  N15: R3.Pin_1, Arduino_MEGA_2560.D11_PWM
  N16: R4.Pin_1, Arduino_MEGA_2560.D2_PWM
  N17: R5.Pin_1, Arduino_MEGA_2560.D3_PWM
  D45: R6.Pin_1, Arduino_MEGA_2560.D45
  N18: R8.Pin_0, U6.Pin_1
  N19: R8.Pin_1, R9.Pin_1, R10.Pin_1, R11.Pin_1, R12.Pin_1, R13.Pin_1, J8.pin1
  N20: R9.Pin_0, U7.Pin_1
  N21: R10.Pin_0, U8.Pin_1
  N22: R11.Pin_0, U9.Pin_1
  N23: R12.Pin_0, U10.Pin_1
  N24: R13.Pin_0, U11.Pin_1
  N25: J8.pin3, U11.Pin_2
  N26: J8.pin4, U10.Pin_2
  N27: J8.pin5, U9.Pin_2
  N28: J8.pin6, U8.Pin_2
  N29: J8.pin7, U7.Pin_2
  N30: J8.pin8, U6.Pin_2
  N31: Q9.B, R7.Pin_0
  N32: U6.Pin_4, Arduino_MEGA_2560.A10
  N33: U7.Pin_4, Arduino_MEGA_2560.A11
  N34: U8.Pin_4, Arduino_MEGA_2560.A12
  N35: U9.Pin_4, Arduino_MEGA_2560.A13
  N36: U10.Pin_4, Arduino_MEGA_2560.A14
  N37: U11.Pin_4, Arduino_MEGA_2560.A15

notes:
  Frederic H-G DIM V2 mai22
  LED1
  LED2
  LED3
  LED4
  LED5
  H_LED
  EXTRA
  Jacob Vautour
  DIM_V2
  2022/05/16
